// Logisim project s-mips.circ as structural Verilog: 16 circuits, main circuit S-MIPS Board
module S_MIPS_Board (
  input  DESHABILITAR_DISPATCHER,
  output halt
);

  wire button_1_out, CLK, CS, d_ff_1_q, LCLR, LoadRAM, LoadRAMOn, LW, R_R_W, R_W, ram_dispatcher_1_finished,
       RCS, Reset_out, RST, TTY_EN;
  wire [2:0] KDB;
  wire [3:0] LMask, Mask, ram_1_read_time, ram_1_write_time, RMask;
  wire [6:0] KDB_DATA, TTY_DATA;
  wire [15:0] Addr, LAddr, RAddr;
  wire [31:0] I0, I1, I2, I3, LData, ram_1_data_out_0, ram_1_data_out_1, ram_1_data_out_2, ram_1_data_out_3,
       RI0, RI1, RI2, RI3;

  TTY #(.rows(25), .cols(80)) tty_1 (.data(TTY_DATA), .clk(CLK), .we(TTY_EN), .clr(RST));
  not not_1 (LoadRAMOn, ram_dispatcher_1_finished);
  RAM_Dispatcher ram_dispatcher_1 (
    .WriteTime(ram_1_write_time), .Clock(CLK), .Data(LData), .Address(LAddr), .Mask(LMask),
    .Finished(ram_dispatcher_1_finished), .Write(LW), .CLR(LCLR));
  Keyboard #(.buflen(64)) keyboard_1 (.clk(CLK), .re(KDB[0]), .avail(KDB[2]), .data(KDB_DATA));  // open: clr
  RAM ram_1 (
    .Address(RAddr), .Data_Out_0(ram_1_data_out_0), .Data_Out_1(ram_1_data_out_1),
    .Data_Out_2(ram_1_data_out_2), .Data_Out_3(ram_1_data_out_3), .Data_In_0(RI0), .Data_In_1(RI1),
    .Data_In_2(RI2), .Data_In_3(RI3), .Mask(RMask), .nRead_Write(R_R_W), .Chip_Select(RCS),
    .Read_Time(ram_1_read_time), .Reset(button_1_out), .Write_Time(ram_1_write_time));
  Button button_1 (.out(button_1_out));
  D_Flip_Flop d_ff_1 (.clk(CLK), .D(1'b1), .Q(d_ff_1_q), .reset(Reset_out));  // open: Qn, preset, en
  Button Reset (.out(Reset_out));
  S_MIPS s_mips_1 (
    .Kbd_Enable(KDB[0]), .Address(Addr), .Kbd_Clear(KDB[1]), .Kbd_Available(KDB[2]), .RAM_In_0(I0),
    .Kbd_ASCII_Data(KDB_DATA), .RAM_In_1(I1), .TTY_Enable(TTY_EN), .RAM_In_2(I2), .RAM_In_3(I3),
    .TTY_ASCII_Data(TTY_DATA), .Reset(RST), .RAM_Out_0(ram_1_data_out_0), .Clock(CLK),
    .RAM_Out_1(ram_1_data_out_1), .Stop(halt), .RAM_Out_2(ram_1_data_out_2), .RAM_Out_3(ram_1_data_out_3),
    .Mask(Mask), .Read_Time(ram_1_read_time), .Write_Time(ram_1_write_time), .nRead_Write(R_W),
    .Chip_Select(CS));
  D_Flip_Flop d_ff_2 (.clk(CLK), .D(d_ff_1_q), .Qn(LCLR), .reset(Reset_out));  // open: Q, preset, en
  or or_1 (RST, LCLR, LoadRAM);
  Clock clock_1 (.out(CLK));
  Multiplexer #(.width(32), .enable("false")) multiplexer_1 (.in0(I0), .in1(LData), .out(RI0), .sel(LoadRAM));
  Multiplexer #(.width(32), .enable("false")) multiplexer_2 (.in0(I1), .in1(LData), .out(RI1), .sel(LoadRAM));
  Multiplexer #(.width(32), .enable("false")) multiplexer_3 (.in0(I2), .in1(LData), .out(RI2), .sel(LoadRAM));
  Multiplexer #(.width(32), .enable("false")) multiplexer_4 (.in0(I3), .in1(LData), .out(RI3), .sel(LoadRAM));
  and and_1 (LoadRAM, ~DESHABILITAR_DISPATCHER, LoadRAMOn);  // AND_Gate
  Multiplexer #(.width(16), .enable("false")) multiplexer_5 (.in0(Addr), .in1(LAddr), .out(RAddr), .sel(LoadRAM));
  Multiplexer #(.width(4), .enable("false")) multiplexer_6 (.in0(Mask), .in1(LMask), .out(RMask), .sel(LoadRAM));
  Multiplexer #(.enable("false")) multiplexer_7 (.in0(CS), .in1(LW), .out(RCS), .sel(LoadRAM));
  Multiplexer #(.enable("false")) multiplexer_8 (.in0(R_W), .in1(LW), .out(R_R_W), .sel(LoadRAM));

  // Notes on the sheet:
  //   NO MODIFICAR
  //   Keyboard
endmodule

module RAM (
  input  [15:0] Address,
  input  [31:0] Data_In_0,
  input  [31:0] Data_In_1,
  input  [31:0] Data_In_2,
  input  [31:0] Data_In_3,
  input  [3:0] Mask,
  input  nRead_Write,
  input  Chip_Select,
  input  Reset,
  output [31:0] Data_Out_0,
  output [31:0] Data_Out_1,
  output [31:0] Data_Out_2,
  output [31:0] Data_Out_3,
  output [3:0] Read_Time,
  output [3:0] Write_Time
);

  wire and_2_out, and_3_out, and_4_out, and_5_out, and_6_out, and_7_out, and_8_out, and_9_out, Changed, CLK,
       comparator_2_eq, comparator_3_eq, comparator_4_eq, comparator_5_eq, comparator_6_eq, Count,
       demultiplexer_3_out0, Idle, Idle_q, Load, Load0, Load1, nand_1_out, or_1_out, or_2_out, or_3_out,
       or_4_out, or_5_out, or_6_out, or_7_out, or_8_out, or_9_out, or_10_out, Proc_q, Update_Mem, Zero_Time;
  wire [3:0] counter_1_q, multiplexer_1_out, subtractor_1_out;
  wire [31:0] register_1_q, register_2_q, register_3_q, register_4_q, register_5_q;

  // Probe on 4'b0011
  // Probe on 4'b0010
  Multiplexer #(.width(4), .enable("false")) multiplexer_1 (
    .in0(4'b0011), .in1(4'b0010), .out(multiplexer_1_out), .sel(nRead_Write));
  or or_1 (or_1_out, Idle, Update_Mem);
  or or_2 (or_2_out, ~Chip_Select, Reset);  // OR_Gate
  Subtractor #(.width(4)) subtractor_1 (.a(multiplexer_1_out), .b(4'b0010), .out(subtractor_1_out));  // open: bin, bout
  D_Flip_Flop u_Idle (.clk(CLK), .D(or_1_out), .Q(Idle_q), .preset(or_2_out));  // open: Qn, en, reset
  Demultiplexer #(.enable("false")) demultiplexer_1 (.out0(Idle), .out1(Load0), .in(Idle_q), .sel(Changed));
  // Probe on counter_1_q
  Counter #(.width(4), .max('hf)) counter_1 (
    .load(Load), .D(subtractor_1_out), .count(Count), .Q(counter_1_q), .clk(CLK), .clr(or_3_out));  // open: carry
  or or_3 (or_3_out, ~Chip_Select, Reset);  // OR_Gate
  Comparator #(.width(4), .mode("unsigned")) comparator_1 (
    .a(4'b0000), .b(counter_1_q), .eq(Zero_Time));  // open: gt, lt
  or or_4 (or_4_out, Count, Load0, Load1);
  Register #(.width(32)) register_1 (.D(Data_In_0), .en(Chip_Select), .Q(register_1_q), .clk(CLK), .clr(or_5_out));
  or or_5 (or_5_out, ~Chip_Select, Reset);  // OR_Gate
  Register #(.width(32)) register_2 (.D(Data_In_1), .en(Chip_Select), .Q(register_2_q), .clk(CLK), .clr(or_6_out));
  or or_6 (or_6_out, ~Chip_Select, Reset);  // OR_Gate
  Register #(.width(32)) register_3 (.D(Data_In_2), .en(Chip_Select), .Q(register_3_q), .clk(CLK), .clr(or_7_out));
  or or_7 (or_7_out, ~Chip_Select, Reset);  // OR_Gate
  Register #(.width(32)) register_4 (.D(Data_In_3), .en(Chip_Select), .Q(register_4_q), .clk(CLK), .clr(or_8_out));
  or or_8 (or_8_out, ~Chip_Select, Reset);  // OR_Gate
  Register #(.width(32)) register_5 (
    .D({{11{1'b1}}, nRead_Write, Mask, Address}), .en(Chip_Select), .Q(register_5_q), .clk(CLK),
    .clr(or_9_out));
  or or_9 (or_9_out, ~Chip_Select, Reset);  // OR_Gate
  D_Flip_Flop Proc (.clk(CLK), .D(or_4_out), .Q(Proc_q), .reset(or_10_out));  // open: Qn, preset, en
  or or_10 (or_10_out, ~Chip_Select, Reset);  // OR_Gate
  Demultiplexer #(.enable("false")) demultiplexer_2 (
    .out0(Count), .out1(Update_Mem), .in(demultiplexer_3_out0), .sel(Zero_Time));
  Demultiplexer #(.enable("false")) demultiplexer_3 (
    .out0(demultiplexer_3_out0), .out1(Load1), .in(Proc_q), .sel(Changed));
  Clock clock_1 (.out(CLK));
  Comparator #(.width(32)) comparator_2 (.a(register_1_q), .b(Data_In_0), .eq(comparator_2_eq));  // open: gt, lt
  Comparator #(.width(32)) comparator_3 (.a(register_2_q), .b(Data_In_1), .eq(comparator_3_eq));  // open: gt, lt
  Comparator #(.width(32)) comparator_4 (.a(register_3_q), .b(Data_In_2), .eq(comparator_4_eq));  // open: gt, lt
  Comparator #(.width(32)) comparator_5 (.a(register_4_q), .b(Data_In_3), .eq(comparator_5_eq));  // open: gt, lt
  Comparator #(.width(32)) comparator_6 (
    .a(register_5_q), .b({{11{1'b1}}, nRead_Write, Mask, Address}), .eq(comparator_6_eq));  // open: gt, lt
  nand nand_1 (nand_1_out, comparator_6_eq, comparator_2_eq, comparator_3_eq, comparator_4_eq, comparator_5_eq);
  and and_1 (Changed, nand_1_out, Chip_Select);
  or or_11 (Load, Count, Load1, Load0);
  and and_2 (and_2_out, Mask[0], Update_Mem, nRead_Write);
  and and_3 (and_3_out, Mask[1], Update_Mem, nRead_Write);
  and and_4 (and_4_out, Mask[2], Update_Mem, nRead_Write);
  and and_5 (and_5_out, Mask[3], Update_Mem, nRead_Write);
  RAM_part #(.addrWidth(16), .dataWidth(32), .bus("separate")) ram_1 (
    .addr(Address), .din(Data_In_0), .data(Data_Out_0), .str(and_2_out), .sel(Chip_Select), .clk(CLK),
    .ld(and_6_out), .clr(Reset));
  and and_6 (and_6_out, ~nRead_Write, Idle);  // AND_Gate
  RAM_part #(.addrWidth(16), .dataWidth(32), .bus("separate")) ram_2 (
    .addr(Address), .din(Data_In_1), .data(Data_Out_1), .str(and_3_out), .sel(Chip_Select), .clk(CLK),
    .ld(and_7_out), .clr(Reset));
  and and_7 (and_7_out, ~nRead_Write, Idle);  // AND_Gate
  RAM_part #(.addrWidth(16), .dataWidth(32), .bus("separate")) ram_3 (
    .addr(Address), .din(Data_In_2), .data(Data_Out_2), .str(and_4_out), .sel(Chip_Select), .clk(CLK),
    .ld(and_8_out), .clr(Reset));
  and and_8 (and_8_out, ~nRead_Write, Idle);  // AND_Gate
  RAM_part #(.addrWidth(16), .dataWidth(32), .bus("separate")) ram_4 (
    .addr(Address), .din(Data_In_3), .data(Data_Out_3), .str(and_5_out), .sel(Chip_Select), .clk(CLK),
    .ld(and_9_out), .clr(Reset));
  and and_9 (and_9_out, ~nRead_Write, Idle);  // AND_Gate

  assign Read_Time = 4'b0011;
  assign Write_Time = 4'b0010;

  // Other names for the same wires on the sheet: M0 = Mask[0]; M1 = Mask[1]; M2 = Mask[2]; M3 = Mask[3];
  //   RW = nRead_Write; CLR = Reset; CS = Chip_Select; Load2 = Count

  // Notes on the sheet:
  //   NO MODIFICAR
  //   excepto quizás los valores RT y WT
  //   BANK0
  //   BANK1
  //   BANK2
  //   BANK3
endmodule

module S_MIPS (
  input  Kbd_Available,
  input  [6:0] Kbd_ASCII_Data,
  input  [31:0] RAM_Out_0,
  input  [31:0] RAM_Out_1,
  input  Reset,
  input  [31:0] RAM_Out_2,
  input  Clock,
  input  [31:0] RAM_Out_3,
  input  [3:0] Read_Time,
  input  [3:0] Write_Time,
  output Kbd_Enable,
  output [15:0] Address,
  output Kbd_Clear,
  output TTY_Enable,
  output [6:0] TTY_ASCII_Data,
  output Stop,
  output [31:0] RAM_In_0,
  output [31:0] RAM_In_1,
  output [31:0] RAM_In_2,
  output [31:0] RAM_In_3,
  output [3:0] Mask,
  output nRead_Write,
  output Chip_Select
);

  wire Cache_R_W, END_Cache, Execute_Ins, Start_Cache;
  wire [31:0] Address_t, Cache_Data, Current_Ins, Input_Bus, Nxt_Ins, R1_Rt, R2_Rd_Offset, RAM_In;
  wire [31:7] R0_Rs;

  Data_Path data_path_1 (
    .Enable(Execute_Ins), .Reset(Reset), .Clock(Clock), .Instruction(Current_Ins), .Input_Data(Input_Bus),
    .Next_Instruction(Nxt_Ins), .Readed_data({R0_Rs, TTY_ASCII_Data}), .Readed_data_2(R1_Rt),
    .Readed_data_3(R2_Rd_Offset));
  Control_Unit control_unit_1 (
    .Kbd_Enable(Kbd_Enable), .RAM_Out_0(Cache_Data), .Kbd_Available(Kbd_Available),
    .Kbd_ASCII_Data(Kbd_ASCII_Data), .Data_Output(Input_Bus), .TTY_Enable(TTY_Enable),
    .TTY_ASCII_Data(TTY_ASCII_Data), .Reset(Reset), .Execute_Instruction(Execute_Ins), .Clock(Clock),
    .Stop(Stop), .Next_Instruction(Nxt_Ins), .Current_Instruction(Current_Ins),
    .R_0({R0_Rs, TTY_ASCII_Data}), .ADDRESS(Address_t), .R_1(R1_Rt), .Start_Cache(Start_Cache),
    .Cache_R_W(Cache_R_W), .R_2(R2_Rd_Offset), .End_Cache(END_Cache));
  Add_Endiannes add_endiannes_1 (.Input(RAM_In), .Output(RAM_In_0));
  Cache_128_bytes cache_128_bytes_1 (
    .Address(Address_t), .Output(Cache_Data), .Clock(Clock), .End(END_Cache), .Reset(Reset),
    .RAM_Address(Address), .Start(Start_Cache), .nR_W(Cache_R_W), .RAM_Input(RAM_In), .CS(Chip_Select),
    .Data_Path_Value(R1_Rt), .nR_W_2(nRead_Write), .RAM_Mask(Mask), .RAM_Output(RAM_Out_0),
    .RAM_Output_2(RAM_Out_1), .RAM_Output_3(RAM_Out_2), .RAM_Output_4(RAM_Out_3), .Read_Time(Read_Time),
    .Write_Time(Write_Time));

  assign Kbd_Clear = Reset;
  assign RAM_In_1 = RAM_In_0;
  assign RAM_In_2 = RAM_In_0;
  assign RAM_In_3 = RAM_In_0;

  // Other names for the same wires on the sheet: CLK = Clock; CS = Chip_Select; KBD_AVAIL = Kbd_Available;
  //   KBD_DATA[6:0] = Kbd_ASCII_Data; R0_Rs[6:0] = TTY_ASCII_Data; TTY_DATA[6:0] = TTY_ASCII_Data;
  //   RAM_A[15:0] = Address; RAM_INPUT_0[31:0] = RAM_In_0; RAM_INPUT_1[31:0] = RAM_In_0; RAM_INPUT_2[31:0] = RAM_In_0;
  //   RAM_INPUT_3[31:0] = RAM_In_0; RAM_MASK[3:0] = Mask; RAM_OUTPUT_0[31:0] = RAM_Out_0;
  //   RAM_OUTPUT_1[31:0] = RAM_Out_1; RAM_OUTPUT_2[31:0] = RAM_Out_2; RAM_OUTPUT_3[31:0] = RAM_Out_3; RST = Reset;
  //   RW = nRead_Write

  // Notes on the sheet:
  //   RAM ADDRESS
  //   DATA FROM RAM
  //   DATA TO RAM
  //   DATA WRITE MASK
  //   RAM TIMING
  //   RAM CONTROL
  //   KEYBOARD
  //   TTY
  //   SEQUENCING
endmodule

module RAM_Dispatcher (
  input  [3:0] WriteTime,
  input  Clock,
  input  CLR,
  output [31:0] Data,
  output [15:0] Address,
  output [3:0] Mask,
  output Finished,
  output Write
);

  wire demultiplexer_2_out1, demultiplexer_3_out1, End, IDLE_q, IncAddr, Load, or_1_out, or_2_out, While_q,
       WriteEnd;
  wire [3:0] counter_1_q;
  wire [31:0] CurrentAddress_q;

  Counter #(.width(32), .max('hffffffff)) CurrentAddress (
    .count(IncAddr), .Q({CurrentAddress_q[31:18], Address, CurrentAddress_q[1:0]}), .clk(Clock), .clr(CLR));  // open: load, D, carry
  or or_1 (or_1_out, IncAddr, demultiplexer_3_out1, Finished);
  D_Flip_Flop IDLE (.clk(Clock), .D(or_1_out), .Q(IDLE_q), .preset(CLR));  // open: Qn, en, reset
  Demultiplexer #(.enable("false")) demultiplexer_1 (.out0(Load), .out1(Finished), .in(IDLE_q), .sel(End));
  D_Flip_Flop While (.clk(Clock), .D(or_2_out), .Q(While_q), .reset(CLR));  // open: Qn, preset, en
  or or_2 (or_2_out, Write, Load);
  RAM_part #(.addrWidth(18), .dataWidth(32)) ram_1 (
    .addr({Address, CurrentAddress_q[1:0]}), .data(Data), .clk(Clock));  // open: sel, ld, clr
  Demultiplexer #(.enable("false")) demultiplexer_2 (
    .out0(Write), .out1(demultiplexer_2_out1), .in(While_q), .sel(WriteEnd));
  Decoder #(.select(2)) decoder_1 (
    .out0(Mask[0]), .out1(Mask[1]), .out2(Mask[2]), .out3(Mask[3]), .sel(CurrentAddress_q[1:0]));  // open: en
  Demultiplexer #(.enable("false")) demultiplexer_3 (
    .out0(IncAddr), .out1(demultiplexer_3_out1), .in(demultiplexer_2_out1), .sel(End));
  Counter #(.width(4), .max('hf)) counter_1 (
    .load(Load), .D(WriteTime), .count(Write), .Q(counter_1_q), .clk(Clock));  // open: carry, clr
  Comparator #(.width(32)) comparator_1 (.a(Data), .b({32{1'b1}}), .eq(End));  // open: gt, lt
  Comparator #(.width(4)) comparator_2 (.a(4'b0000), .b(counter_1_q), .eq(WriteEnd));  // open: gt, lt

  // Other names for the same wires on the sheet: CLK = Clock; Count = Write; WT[3:0] = WriteTime
endmodule

module Register_File (
  input  Write_1___Read_0,
  input  Reset,
  input  Clock,
  input  [31:0] in_4,
  input  [4:0] S__Output_A,
  input  [4:0] S__Output_B,
  input  [4:0] S__Register_to_Write,
  output [31:0] Output_A,
  output [31:0] Output_B
);

  wire R0, R1, R2, R3, R4, R5, R6, R7, R8, R9, R10, R11, R12, R13, R14, R15, R16, R17, R18, R19, R20, R21,
       R22, R23, R24, R25, R26, R27, R28, R29, R30, R31;
  wire [31:0] OutP_0, OutP_1, OutP_2, OutP_3, OutP_4, OutP_5, OutP_6, OutP_7, OutP_8, OutP_9, OutP_10,
       OutP_11, OutP_12, OutP_13, OutP_14, OutP_15, OutP_16, OutP_17, OutP_18, OutP_19, OutP_20, OutP_21,
       OutP_22, OutP_23, OutP_24, OutP_25, OutP_26, OutP_27, OutP_28, OutP_29, OutP_30, OutP_31;

  Multiplexer #(.select(5), .width(32), .enable("false")) multiplexer_1 (
    .in0(OutP_0), .in1(OutP_1), .in2(OutP_2), .in3(OutP_3), .in4(OutP_4), .in5(OutP_5), .in6(OutP_6),
    .in7(OutP_7), .in8(OutP_8), .in9(OutP_9), .in10(OutP_10), .in11(OutP_11), .in12(OutP_12), .in13(OutP_13),
    .in14(OutP_14), .in15(OutP_15), .in16(OutP_16), .in17(OutP_17), .in18(OutP_18), .in19(OutP_19),
    .in20(OutP_20), .in21(OutP_21), .in22(OutP_22), .in23(OutP_23), .in24(OutP_24), .in25(OutP_25),
    .in26(OutP_26), .in27(OutP_27), .in28(OutP_28), .in29(OutP_29), .in30(OutP_30), .in31(OutP_31),
    .out(Output_A), .sel(S__Output_A));
  Demultiplexer #(.select(5), .enable("false")) demultiplexer_1 (
    .out0(R0), .out1(R1), .out2(R2), .out3(R3), .out4(R4), .out5(R5), .out6(R6), .out7(R7), .out8(R8),
    .out9(R9), .out10(R10), .out11(R11), .out12(R12), .out13(R13), .out14(R14), .out15(R15), .out16(R16),
    .out17(R17), .out18(R18), .out19(R19), .out20(R20), .out21(R21), .out22(R22), .out23(R23), .out24(R24),
    .out25(R25), .out26(R26), .out27(R27), .out28(R28), .out29(R29), .out30(R30), .out31(R31),
    .in(Write_1___Read_0), .sel(S__Register_to_Write));
  Multiplexer #(.select(5), .width(32), .enable("false")) multiplexer_2 (
    .in0(OutP_0), .in1(OutP_1), .in2(OutP_2), .in3(OutP_3), .in4(OutP_4), .in5(OutP_5), .in6(OutP_6),
    .in7(OutP_7), .in8(OutP_8), .in9(OutP_9), .in10(OutP_10), .in11(OutP_11), .in12(OutP_12), .in13(OutP_13),
    .in14(OutP_14), .in15(OutP_15), .in16(OutP_16), .in17(OutP_17), .in18(OutP_18), .in19(OutP_19),
    .in20(OutP_20), .in21(OutP_21), .in22(OutP_22), .in23(OutP_23), .in24(OutP_24), .in25(OutP_25),
    .in26(OutP_26), .in27(OutP_27), .in28(OutP_28), .in29(OutP_29), .in30(OutP_30), .in31(OutP_31),
    .out(Output_B), .sel(S__Output_B));
  Register #(.width(32)) u_R0 (.D({32{1'b0}}), .en(R0), .Q(OutP_0), .clk(Clock), .clr(Reset));
  Register #(.width(32)) u_R5 (.D(in_4), .en(R5), .Q(OutP_5), .clk(Clock), .clr(Reset));
  Register #(.width(32)) u_R10 (.D(in_4), .en(R10), .Q(OutP_10), .clk(Clock), .clr(Reset));
  Register #(.width(32)) u_R15 (.D(in_4), .en(R15), .Q(OutP_15), .clk(Clock), .clr(Reset));
  Register #(.width(32)) u_R20 (.D(in_4), .en(R20), .Q(OutP_20), .clk(Clock), .clr(Reset));
  Register #(.width(32)) u_R25 (.D(in_4), .en(R25), .Q(OutP_25), .clk(Clock), .clr(Reset));
  Register #(.width(32)) u_R30 (.D(in_4), .en(R30), .Q(OutP_30), .clk(Clock), .clr(Reset));
  Register #(.width(32)) u_R1 (.D(in_4), .en(R1), .Q(OutP_1), .clk(Clock), .clr(Reset));
  Register #(.width(32)) u_R6 (.D(in_4), .en(R6), .Q(OutP_6), .clk(Clock), .clr(Reset));
  Register #(.width(32)) u_R11 (.D(in_4), .en(R11), .Q(OutP_11), .clk(Clock), .clr(Reset));
  Register #(.width(32)) u_R16 (.D(in_4), .en(R16), .Q(OutP_16), .clk(Clock), .clr(Reset));
  Register #(.width(32)) u_R21 (.D(in_4), .en(R21), .Q(OutP_21), .clk(Clock), .clr(Reset));
  Register #(.width(32)) u_R26 (.D(in_4), .en(R26), .Q(OutP_26), .clk(Clock), .clr(Reset));
  Register #(.width(32)) R31___Stack_Pointer (.D(in_4), .en(R31), .Q(OutP_31), .clk(Clock), .clr(Reset));
  Register #(.width(32)) u_R2 (.D(in_4), .en(R2), .Q(OutP_2), .clk(Clock), .clr(Reset));
  Register #(.width(32)) u_R7 (.D(in_4), .en(R7), .Q(OutP_7), .clk(Clock), .clr(Reset));
  Register #(.width(32)) u_R12 (.D(in_4), .en(R12), .Q(OutP_12), .clk(Clock), .clr(Reset));
  Register #(.width(32)) u_R17 (.D(in_4), .en(R17), .Q(OutP_17), .clk(Clock), .clr(Reset));
  Register #(.width(32)) u_R22 (.D(in_4), .en(R22), .Q(OutP_22), .clk(Clock), .clr(Reset));
  Register #(.width(32)) u_R27 (.D(in_4), .en(R27), .Q(OutP_27), .clk(Clock), .clr(Reset));
  Register #(.width(32)) u_R3 (.D(in_4), .en(R3), .Q(OutP_3), .clk(Clock), .clr(Reset));
  Register #(.width(32)) u_R8 (.D(in_4), .en(R8), .Q(OutP_8), .clk(Clock), .clr(Reset));
  Register #(.width(32)) u_R13 (.D(in_4), .en(R13), .Q(OutP_13), .clk(Clock), .clr(Reset));
  Register #(.width(32)) u_R18 (.D(in_4), .en(R18), .Q(OutP_18), .clk(Clock), .clr(Reset));
  Register #(.width(32)) u_R23 (.D(in_4), .en(R23), .Q(OutP_23), .clk(Clock), .clr(Reset));
  Register #(.width(32)) u_R28 (.D(in_4), .en(R28), .Q(OutP_28), .clk(Clock), .clr(Reset));
  Register #(.width(32)) u_R4 (.D(in_4), .en(R4), .Q(OutP_4), .clk(Clock), .clr(Reset));
  Register #(.width(32)) u_R9 (.D(in_4), .en(R9), .Q(OutP_9), .clk(Clock), .clr(Reset));
  Register #(.width(32)) u_R14 (.D(in_4), .en(R14), .Q(OutP_14), .clk(Clock), .clr(Reset));
  Register #(.width(32)) u_R19 (.D(in_4), .en(R19), .Q(OutP_19), .clk(Clock), .clr(Reset));
  Register #(.width(32)) u_R24 (.D(in_4), .en(R24), .Q(OutP_24), .clk(Clock), .clr(Reset));
  Register #(.width(32)) u_R29 (.D(in_4), .en(R29), .Q(OutP_29), .clk(Clock), .clr(Reset));

  // Other names for the same wires on the sheet: Clk = Clock; Input[31:0] = in_4; R = Reset; S_A[4:0] = S__Output_A;
  //   S_B[4:0] = S__Output_B; S_R_W[4:0] = S__Register_to_Write; W_R = Write_1___Read_0

  // Notes on the sheet:
  //   Selector of Register to Write
  //   Registers
endmodule

module ALU (
  input  [31:0] Num_A,
  input  [31:0] Num_B,
  input  [3:0] S__Operation,
  output [31:0] Outp__A_Op_B,
  output [31:0] Aux__Outp__A_Op_B
);

  wire comparator_1_lt, comparator_2_lt;
  wire [31:0] Add, And, Div, Div_Rest, Divu, Divu_Rest, Mult_H0, Mult_L0, Mulu_H0, Mulu_L0, Nor, Or, SLT,
       STLU, Sub, Xor;

  Adder #(.width(32)) adder_1 (.a(Num_A), .b(Num_B), .out(Add));  // open: cin, cout
  Subtractor #(.width(32)) subtractor_1 (.a(Num_A), .b(Num_B), .out(Sub));  // open: bin, bout
  Multiplier #(.width(32)) multiplier_1 (.a(Num_A), .b(Num_B), .out(Mult_L0), .cout(Mult_H0));  // open: cin
  Unsigned_Mult unsigned_mult_1 (.in_1(Num_B), .in_2(Num_A), .Outp__Low(Mulu_L0), .Outp__High(Mulu_H0));
  Signed_Div signed_div_1 (.in_1(Num_A), .in_2(Num_B), .Output_L(Div), .Output_H(Div_Rest));
  Divider #(.width(32)) divider_1 (.a(Num_A), .b(Num_B), .out(Divu), .upper({32{1'b0}}), .rem(Divu_Rest));
  assign And = Num_A & Num_B;  // AND_Gate And, 32 bits wide
  assign Or = Num_A | Num_B;  // OR_Gate Or, 32 bits wide
  assign Nor = ~(Num_A | Num_B);  // NOR_Gate Nor, 32 bits wide
  assign Xor = Num_A ^ Num_B;  // XOR_Gate Xor, 32 bits wide
  Comparator #(.width(32)) comparator_1 (.a(Num_A), .b(Num_B), .lt(comparator_1_lt));  // open: gt, eq
  Comparator #(.width(32), .mode("unsigned")) comparator_2 (
    .a(Num_A), .b(Num_B), .lt(comparator_2_lt));  // open: gt, eq
  assign SLT = {{31{1'b0}}, comparator_1_lt};  // Bit_Extender bit_extender_1
  assign STLU = {{31{1'b0}}, comparator_2_lt};  // Bit_Extender bit_extender_2
  Multiplexer #(.select(4), .width(32), .enable("false")) multiplexer_1 (
    .in0(Add), .in1(Sub), .in2(SLT), .in3(STLU), .in4(And), .in5(Or), .in6(Xor), .in7(Nor), .in8(Mult_L0),
    .in9(Div), .in10(Mulu_L0), .in11(Divu), .in12({32{1'b0}}), .in13({32{1'b0}}), .in14({32{1'b0}}),
    .in15({32{1'b0}}), .out(Outp__A_Op_B), .sel(S__Operation));
  Multiplexer #(.select(4), .width(32), .enable("false")) multiplexer_2 (
    .in0({32{1'b0}}), .in1({32{1'b0}}), .in2({32{1'b0}}), .in3({32{1'b0}}), .in4({32{1'b0}}),
    .in5({32{1'b0}}), .in6({32{1'b0}}), .in7({32{1'b0}}), .in8(Mult_H0), .in9(Div_Rest), .in10(Mulu_H0),
    .in11(Divu_Rest), .in12({32{1'b0}}), .in13({32{1'b0}}), .in14({32{1'b0}}), .in15({32{1'b0}}),
    .out(Aux__Outp__A_Op_B), .sel(S__Operation));

  // Other names for the same wires on the sheet: A[31:0] = Num_A; B[31:0] = Num_B; S__Op[3:0] = S__Operation

  // Notes on the sheet:
  //   STL
  //   STLU
endmodule

module Unsigned_Mult (
  input  [31:0] in_1,
  input  [31:0] in_2,
  output [31:0] Outp__Low,
  output [31:0] Outp__High
);

  wire adder_1_cout, adder_3_cout;
  wire [31:0] a__inferior, a__superior, adder_1_out, adder_2_out, b__inferior, b__superior, inferior,
       inferior_t, superior, superior_1, superior_2;
  wire [31:16] inferior_1, inferior_2, multiplier_1_out, multiplier_2_out;

  assign a__inferior = {{16{1'b0}}, in_1[15:0]};  // Bit_Extender bit_extender_1
  assign a__superior = {{16{1'b0}}, in_1[31:16]};  // Bit_Extender bit_extender_2
  Multiplier #(.width(32)) multiplier_1 (
    .a(a__superior), .b(b__inferior), .out({multiplier_1_out, inferior_1}));  // open: cin, cout
  Multiplier #(.width(32)) multiplier_2 (
    .a(a__inferior), .b(b__superior), .out({multiplier_2_out, inferior_2}));  // open: cin, cout
  assign b__inferior = {{16{1'b0}}, in_2[15:0]};  // Bit_Extender bit_extender_3
  assign b__superior = {{16{1'b0}}, in_2[31:16]};  // Bit_Extender bit_extender_4
  assign superior_1 = {{16{1'b0}}, multiplier_1_out};  // Bit_Extender bit_extender_5
  assign superior_2 = {{16{1'b0}}, multiplier_2_out};  // Bit_Extender bit_extender_6
  Multiplier #(.width(32)) multiplier_3 (.a(a__superior), .b(b__superior), .out(superior));  // open: cin, cout
  Multiplier #(.width(32)) multiplier_4 (.a(a__inferior), .b(b__inferior), .out(inferior));  // open: cin, cout
  Adder #(.width(32)) adder_1 (
    .a(inferior_t), .b({inferior_1, {16{1'b0}}}), .out(adder_1_out), .cout(adder_1_cout));  // open: cin
  Adder #(.width(32)) adder_2 (.a(superior_1), .b(superior_2), .out(adder_2_out), .cin(adder_1_cout));  // open: cout
  Adder #(.width(32)) adder_3 (
    .a(adder_1_out), .b({inferior_2, {16{1'b0}}}), .out(Outp__Low), .cout(adder_3_cout));  // open: cin
  Adder #(.width(32)) adder_4 (.a(adder_2_out), .b(superior), .out(Outp__High), .cin(adder_3_cout));  // open: cout

  // Other names for the same wires on the sheet: res_inferior[31:0] = Outp__Low; res_superior[31:0] = Outp__High

  // Notes on the sheet:
  //   Resultados:
  //   A dividido en sup. e inf. extendidos cada uno a 32 bits
  //   Formula: A*B = (a*2^k + n) * (b*2^k + m) = a*b*2^[2k] + m*a*2^k + n*b*2^k + n*m 
  //   Distributiva y queda la suma de 4 multiplicaciones. Luego para resolver el signo:
  //   Los bits que se extienden son de 16 a 32 bits, rellenando los bits de 16 a 31 con 0.
  //   a*2^k son los bits superiores de A, b*2^k son los bits superiores de b, n los bits inferiores de A y m los bits inferiores de B.
  //   En complemento A2 si el ultimo bit es 1 ese num tiene signo negativo, por eso se rellenan desde el 16 hasta el ultimo 31 con 0.
  //   De esa forma a, b superiores y a, b inferiores son positivos y se pueden multiplicar usando el mult.
  //   m* a*2^k
  //   n * b*2^k
  //   B dividido en sup. e inf. extendidos cada uno a 32 bits
  //   a*b*2^(2k)
  //   n*m
  //   a*b*2^(2k) + m*a*2^k + n*b*2^k + n*m  
endmodule

module Signed_Div (
  input  [31:0] in_1,
  input  [31:0] in_2,
  output [31:0] Output_L,
  output [31:0] Output_H
);

  wire Signo_Resultante;
  wire [31:0] A_positivo, B_positivo, divider_1_out, divider_1_rem;

  Controlar_Comp__A2 controlar_comp_a2_1 (.num(in_1), .Control(in_1[31]), .Output(A_positivo));
  Controlar_Comp__A2 controlar_comp_a2_2 (.num(in_2), .Control(in_2[31]), .Output(B_positivo));
  Divider #(.width(32)) divider_1 (
    .a(A_positivo), .b(B_positivo), .out(divider_1_out), .rem(divider_1_rem));  // open: upper
  xor xor_1 (Signo_Resultante, in_1[31], in_2[31]);
  Controlar_Comp__A2 controlar_comp_a2_3 (.num(divider_1_out), .Control(Signo_Resultante), .Output(Output_L));
  Controlar_Comp__A2 controlar_comp_a2_4 (.num(divider_1_rem), .Control(Signo_Resultante), .Output(Output_H));

  // Other names for the same wires on the sheet: Signo_Original_A = in_1[31]; Signo_Original_B = in_2[31]

  // Notes on the sheet:
  //   Si el bit 31 es 1 entonces es negativo y se le pasa ese bit como controlador.
  //   Esto es para el signo resultante
  //   Aqui segun el signo resultante se le cambia el signo o no.
endmodule

module Controlar_Comp__A2 (
  input  [31:0] num,
  input  Control,
  output [31:0] Output
);

  wire not_1_out;
  wire [31:0] controlled_buffer_1_out;

  not not_1 (not_1_out, Control);
  assign controlled_buffer_1_out = not_1_out ? num : 32'bz;  // Controlled_Buffer controlled_buffer_1
  assign controlled_buffer_1_out = Control ? ~num : 32'bz;  // Controlled_Inverter controlled_inverter_1
  Adder #(.width(32)) adder_1 (.a(controlled_buffer_1_out), .b({32{1'b0}}), .out(Output), .cin(Control));  // open: cout
endmodule

module Branch_Control (
  input  [5:0] Jmp_Inst,
  input  [31:0] Source,
  input  [31:0] Jmp_Length,
  input  [31:0] Destino,
  input  [31:0] A,
  input  [31:0] B,
  output [31:0] Next
);

  wire Condition, Equal, Great, Less, LessOrEqual, not_1_out;
  wire [31:0] adder_2_out, Conditional_jmp, Inconditional_jmp, Jmp_Length_t, shifter_1_out;

  Comparator #(.width(32)) comparator_1 (.a(A), .b(B), .gt(Great), .eq(Equal), .lt(Less));
  Shifter #(.width(32)) shifter_1 (.in(Jmp_Length), .\dist (5'b00010), .out(shifter_1_out));
  Adder #(.width(32)) adder_1 (.a(shifter_1_out), .b(32'h4), .out(Jmp_Length_t));  // open: cin, cout
  or or_1 (LessOrEqual, Equal, Less);
  Adder #(.width(32)) adder_2 (.a(32'h4), .b(Source), .out(adder_2_out));  // open: cin, cout
  Adder #(.width(32)) adder_3 (.a(Jmp_Length_t), .b(Source), .out(Conditional_jmp));  // open: cin, cout
  Multiplexer #(.select(3), .width(32), .enable("false")) multiplexer_1 (
    .in0(Destino), .in1(adder_2_out), .in2(Destino), .in3(adder_2_out), .in4(adder_2_out), .in5(adder_2_out),
    .in6(adder_2_out), .in7(adder_2_out), .out(Inconditional_jmp), .sel(Jmp_Inst[2:0]));
  Multiplexer #(.select(3), .enable("false")) multiplexer_2 (
    .in0(1'b0), .in1(Less), .in2(1'b0), .in3(1'b0), .in4(Equal), .in5(not_1_out), .in6(LessOrEqual),
    .in7(Great), .out(Condition), .sel(Jmp_Inst[2:0]));
  not not_1 (not_1_out, Equal);
  Multiplexer #(.width(32), .enable("false")) multiplexer_3 (
    .in0(Inconditional_jmp), .in1(Conditional_jmp), .out(Next), .sel(Condition));

  // Other names for the same wires on the sheet: Dest[31:0] = Destino; Inst[2:0] = Jmp_Inst[2:0]; Src[31:0] = Source
endmodule

module Program_Count (
  input  clock,
  input  [31:0] data,
  input  reset,
  output [31:0] Output
);

  Register #(.width(32)) register_1 (.D(data), .Q(Output), .clk(clock), .clr(reset));  // open: en

  // Other names for the same wires on the sheet: CLK = clock; RST = reset
endmodule

module Add_Endiannes (
  input  [31:0] Input,
  output [31:0] Output
);


  assign Output = {Input[7:0], Input[15:8], Input[23:16], Input[31:24]};

  // Other names for the same wires on the sheet: _3[7:0] = Input[31:24]; _2[7:0] = Input[23:16];
  //   _1[7:0] = Input[15:8]; _0[7:0] = Input[7:0]
endmodule

module Instruction_Decoder (
  input  [31:0] Instruction,
  output [5:0] Branch_Op,
  output Random,
  output Take_Input,
  output [3:0] ALU_Op,
  output Move_f__high,
  output Move_f__low,
  output Inmediate_Op,
  output [31:0] Const,
  output Write_to_Hi_Low,
  output Jump_Register,
  output Memory_Get,
  output Memory_Set,
  output Push_Pop,
  output [4:0] Register_Address_0,
  output [4:0] Register_Address_1,
  output [4:0] Register_Address_2
);

  wire add, \and , and_1_out, and_12_out, Branch_Instruction, comparator_16_eq, comparator_17_eq,
       comparator_18_eq, comparator_19_eq, comparator_20_eq, comparator_21_eq, comparator_22_eq,
       comparator_23_lt, comparator_25_gt, div, divu, Enable_ALU, j, kbd, LW, Memory_Inst, mul, mulu, \nor ,
       not_1_out, not_2_out, Ones, \or , or_1_out, or_2_out, or_3_out, or_4_out, or_8_out, Pop,
       priority_encoder_1_en_out, Push, push_tty, rnd, slt, sltu, sub, SW, Type_I, Type_R, \xor , Zero;
  wire [3:0] ALU_Inmediate_Op, ALU_Op_t, multiplexer_8_out, multiplexer_12_out;
  wire [4:0] Memory_Addr, Memory_Data, multiplexer_4_out, multiplexer_5_out;
  wire [5:0] multiplexer_11_out;
  wire [31:0] Const_t, Jmp_Dest, Memory_Const, multiplexer_10_out;

  Multiplexer #(.width(5), .enable("false")) multiplexer_1 (
    .in0({5{1'b0}}), .in1(Instruction[15:11]), .out(Register_Address_2), .sel(Type_R));
  Multiplexer #(.width(5), .enable("false")) multiplexer_2 (
    .in0(multiplexer_4_out), .in1(Memory_Addr), .out(Register_Address_0), .sel(Memory_Inst));
  Multiplexer #(.width(5), .enable("false")) multiplexer_3 (
    .in0(multiplexer_5_out), .in1(Memory_Data), .out(Register_Address_1), .sel(Memory_Inst));
  Multiplexer #(.width(5), .enable("false")) multiplexer_4 (
    .in0({5{1'b0}}), .in1(Instruction[25:21]), .out(multiplexer_4_out), .sel(not_1_out));
  Multiplexer #(.width(5), .enable("false")) multiplexer_5 (
    .in0({5{1'b0}}), .in1(Instruction[20:16]), .out(multiplexer_5_out), .sel(not_2_out));
  Comparator #(.width(6), .mode("unsigned")) comparator_1 (
    .a(Instruction[5:0]), .b(6'b100000), .eq(add));  // open: gt, lt
  Comparator #(.width(6), .mode("unsigned")) comparator_2 (
    .a(Instruction[5:0]), .b(6'b100010), .eq(sub));  // open: gt, lt
  Comparator #(.width(6), .mode("unsigned")) comparator_3 (
    .a(Instruction[5:0]), .b(6'b011000), .eq(mul));  // open: gt, lt
  Comparator #(.width(6), .mode("unsigned")) comparator_4 (
    .a(Instruction[5:0]), .b(6'b011001), .eq(mulu));  // open: gt, lt
  Comparator #(.width(6), .mode("unsigned")) comparator_5 (
    .a(Instruction[5:0]), .b(6'b011010), .eq(div));  // open: gt, lt
  Comparator #(.width(6), .mode("unsigned")) comparator_6 (
    .a(Instruction[5:0]), .b(6'b011011), .eq(divu));  // open: gt, lt
  Comparator #(.width(6), .mode("unsigned")) comparator_7 (
    .a(Instruction[5:0]), .b(6'b101010), .eq(slt));  // open: gt, lt
  Comparator #(.width(6), .mode("unsigned")) comparator_8 (
    .a(Instruction[5:0]), .b(6'b101011), .eq(sltu));  // open: gt, lt
  Comparator #(.width(6), .mode("unsigned")) comparator_9 (
    .a(Instruction[5:0]), .b(6'b100100), .eq(\and ));  // open: gt, lt
  Comparator #(.width(6), .mode("unsigned")) comparator_10 (
    .a(Instruction[5:0]), .b(6'b100101), .eq(\or ));  // open: gt, lt
  Comparator #(.width(6), .mode("unsigned")) comparator_11 (
    .a(Instruction[5:0]), .b(6'b100111), .eq(\nor ));  // open: gt, lt
  Comparator #(.width(6), .mode("unsigned")) comparator_12 (
    .a(Instruction[5:0]), .b(6'b101000), .eq(\xor ));  // open: gt, lt
  not not_1 (not_1_out, j);
  not not_2 (not_2_out, j);
  Multiplexer #(.width(4), .enable("false")) multiplexer_6 (
    .in0(multiplexer_8_out), .in1(4'b0000), .out(ALU_Op), .sel(Memory_Inst));
  Multiplexer #(.width(6), .enable("false")) multiplexer_7 (
    .in0(multiplexer_11_out), .in1(Instruction[31:26]), .out(Branch_Op), .sel(Branch_Instruction));
  Multiplexer #(.width(4), .enable("false")) multiplexer_8 (
    .in0(multiplexer_12_out), .in1(ALU_Inmediate_Op), .out(multiplexer_8_out), .sel(Inmediate_Op));
  Multiplexer #(.width(32), .enable("false")) multiplexer_9 (
    .in0(multiplexer_10_out), .in1(Const_t), .out(Const), .sel(Type_I));
  or or_1 (or_1_out, LW, SW);
  Multiplexer #(.width(32), .enable("false")) multiplexer_10 (
    .in0({32{1'b0}}), .in1(Jmp_Dest), .out(multiplexer_10_out), .sel(j));
  assign Memory_Addr = Push_Pop ? {5{1'b1}} : 5'bz;  // Controlled_Buffer controlled_buffer_1
  assign Memory_Addr = or_1_out ? Instruction[25:21] : 5'bz;  // Controlled_Buffer controlled_buffer_2
  Multiplexer #(.width(6), .enable("false")) multiplexer_11 (
    .in0(6'b000011), .in1(Instruction[5:0]), .out(multiplexer_11_out), .sel(Jump_Register));
  Multiplexer #(.width(4), .enable("false")) multiplexer_12 (
    .in0(4'b0000), .in1(ALU_Op_t), .out(multiplexer_12_out), .sel(and_1_out));
  not not_3 (Enable_ALU, priority_encoder_1_en_out);
  Priority_Encoder #(.select(4)) priority_encoder_1 (
    .in0(add), .in1(sub), .in2(slt), .in3(sltu), .in4(\and ), .in5(\or ), .in6(\xor ), .in7(\nor ),
    .in8(mul), .in9(div), .in10(mulu), .in11(divu), .in12(1'b0), .in13(1'b0), .in14(1'b0), .in15(1'b0),
    .out(ALU_Op_t), .en_out(priority_encoder_1_en_out));  // open: gs, en_in
  Comparator #(.width(6), .mode("unsigned")) comparator_13 (
    .a(Instruction[31:26]), .b({6{1'b0}}), .eq(Zero));  // open: gt, lt
  Comparator #(.width(6), .mode("unsigned")) comparator_14 (
    .a(Instruction[31:26]), .b({6{1'b1}}), .eq(Ones));  // open: gt, lt
  Comparator #(.width(6), .mode("unsigned")) comparator_15 (
    .a(Instruction[31:26]), .b(6'b111000), .eq(Push_Pop));  // open: gt, lt
  and and_1 (and_1_out, Enable_ALU, Zero);
  assign Memory_Data = Push ? Instruction[25:21] : 5'bz;  // Controlled_Buffer controlled_buffer_3
  assign Memory_Data = or_2_out ? Instruction[20:16] : 5'bz;  // Controlled_Buffer controlled_buffer_4
  or or_2 (or_2_out, LW, SW);
  assign Memory_Data = Pop ? Instruction[20:16] : 5'bz;  // Controlled_Buffer controlled_buffer_5
  assign Memory_Const = Push_Pop ? {32{1'b0}} : 32'bz;  // Controlled_Buffer controlled_buffer_6
  assign Memory_Const = or_3_out ? Const_t : 32'bz;  // Controlled_Buffer controlled_buffer_7
  or or_3 (or_3_out, LW, SW);
  or or_4 (or_4_out, mul, div, mulu, divu);
  Comparator #(.width(6), .mode("unsigned")) comparator_16 (
    .a(Instruction[5:0]), .b({6{1'b0}}), .eq(comparator_16_eq));  // open: gt, lt
  Comparator #(.width(6), .mode("unsigned")) comparator_17 (
    .a(Instruction[5:0]), .b(6'b000001), .eq(comparator_17_eq));  // open: gt, lt
  Comparator #(.width(6), .mode("unsigned")) comparator_18 (
    .a(Instruction[5:0]), .b(6'b001000), .eq(comparator_18_eq));  // open: gt, lt
  Comparator #(.width(6), .mode("unsigned")) comparator_19 (
    .a(Instruction[5:0]), .b(6'b010000), .eq(comparator_19_eq));  // open: gt, lt
  Comparator #(.width(6), .mode("unsigned")) comparator_20 (
    .a(Instruction[5:0]), .b(6'b010010), .eq(comparator_20_eq));  // open: gt, lt
  Comparator #(.width(6), .mode("unsigned")) comparator_21 (
    .a(Instruction[5:0]), .b(6'b000010), .eq(comparator_21_eq));  // open: gt, lt
  Comparator #(.width(6), .mode("unsigned")) comparator_22 (
    .a(Instruction[5:0]), .b(6'b000100), .eq(comparator_22_eq));  // open: gt, lt
  assign Const_t = {{16{Instruction[15]}}, Instruction[15:0]};  // Bit_Extender bit_extender_1
  assign Jmp_Dest = {{6{Instruction[25]}}, Instruction[25:0]};  // Bit_Extender bit_extender_2
  and and_2 (Pop, comparator_16_eq, Push_Pop, Type_R);
  and and_3 (push_tty, comparator_17_eq, Type_R);
  and and_4 (Jump_Register, comparator_18_eq, Type_R);
  and and_5 (Move_f__high, comparator_19_eq, Type_R);
  and and_6 (Move_f__low, comparator_20_eq, Type_R);
  and and_7 (rnd, comparator_21_eq, Type_R);
  and and_8 (kbd, comparator_22_eq, Type_R);
  and and_9 (Push, Push_Pop, ~Pop);  // AND_Gate
  and and_10 (Write_to_Hi_Low, or_4_out, Type_R);
  or or_5 (Memory_Inst, Push_Pop, LW, SW);
  or or_6 (Memory_Get, Pop, LW);
  or or_7 (Memory_Set, Push, SW);
  or or_8 (or_8_out, Pop, kbd);
  and and_11 (Random, rnd, Type_R);
  and and_12 (and_12_out, or_8_out, Push_Pop, Type_R);
  or or_9 (Take_Input, and_12_out, LW);
  Comparator #(.width(6), .mode("unsigned")) comparator_23 (
    .a(Instruction[31:26]), .b(6'b101100), .lt(comparator_23_lt));  // open: gt, eq
  Comparator #(.width(6), .mode("unsigned")) comparator_24 (
    .a(Instruction[31:26]), .b(6'b000010), .eq(j));  // open: gt, lt
  Comparator #(.width(6), .mode("unsigned")) comparator_25 (
    .a(Instruction[31:26]), .b({6{1'b0}}), .gt(comparator_25_gt));  // open: eq, lt
  nor u_NOR (Type_R, Type_I, j);
  and and_13 (Inmediate_Op, Instruction[29], Type_I);
  Subtractor #(.width(4)) subtractor_1 (
    .a(Instruction[29:26]), .b(4'b1000), .out(ALU_Inmediate_Op));  // open: bin, bout
  Comparator #(.width(6), .mode("unsigned")) comparator_26 (
    .a(Instruction[31:26]), .b(6'b101011), .eq(SW));  // open: gt, lt
  Comparator #(.width(6), .mode("unsigned")) comparator_27 (
    .a(Instruction[31:26]), .b(6'b100011), .eq(LW));  // open: gt, lt
  nor NOR_2 (Branch_Instruction, SW, LW, Inmediate_Op, Type_R);
  and and_14 (Type_I, comparator_23_lt, ~j, comparator_25_gt);  // AND_Gate

  // Other names for the same wires on the sheet: ALU_Inmediate = Inmediate_Op; Func_Code[5:0] = Instruction[5:0];
  //   Ins[31:0] = Instruction; R_2[4:0] = Instruction[15:11]; R_1[4:0] = Instruction[20:16];
  //   R_0[4:0] = Instruction[25:21]; OpCode[5:0] = Instruction[31:26]; jr = Jump_Register; mfhi = Move_f__high;
  //   mflo = Move_f__low; Rand = Random

  // Notes on the sheet:
  //   Inputs
  //   Output Flags
  //   Instruccion tipo R
  //   Instruccion tipo I
  //   Instruccion tipo J
endmodule

module Data_Path (
  input  Enable,
  input  [31:0] Instruction,
  input  [31:0] Input_Data,
  input  Reset,
  input  Clock,
  output [31:0] Next_Instruction,
  output [31:0] Readed_data,
  output [31:0] Readed_data_2,
  output [31:0] Readed_data_3
);

  wire ALU_Select, and_2_out, and_5_out, and_6_out, and_7_out, Inmediate_Op, Inp, JR, Memory_Get, Memory_Set,
       mfhi, mflo, NOR_out, or_1_out, Out_Select, PC_Select, Push_Pop, R_W_Select, Rf__Select, rnd,
       Write_to_Hi_Lo;
  wire [3:0] ALU_Op;
  wire [4:0] multiplexer_4_out, Register__0, Register__1, Register__2;
  wire [5:0] Branch_Op;
  wire [31:0] ALU_Aux, ALU_Out, branch_control_1_next, Data_Bus, hi, lo, multiplexer_1_out,
       multiplexer_2_out, R_0, Random, shifter_1_out;

  assign Data_Bus = mfhi ? hi : 32'bz;  // Controlled_Buffer controlled_buffer_1
  assign Data_Bus = rnd ? Random : 32'bz;  // Controlled_Buffer controlled_buffer_2
  assign Data_Bus = mflo ? lo : 32'bz;  // Controlled_Buffer controlled_buffer_3
  assign Data_Bus = Inp ? Input_Data : 32'bz;  // Controlled_Buffer controlled_buffer_4
  and and_1 (R_W_Select, Enable, ~Memory_Set);  // AND_Gate
  Instruction_Decoder instruction_decoder_1 (
    .Instruction(Instruction), .Branch_Op(Branch_Op), .Random(rnd), .Take_Input(Inp), .ALU_Op(ALU_Op),
    .Move_f__high(mfhi), .Move_f__low(mflo), .Inmediate_Op(Inmediate_Op), .Const(Readed_data_3),
    .Write_to_Hi_Low(Write_to_Hi_Lo), .Jump_Register(JR), .Memory_Get(Memory_Get), .Memory_Set(Memory_Set),
    .Push_Pop(Push_Pop), .Register_Address_0(Register__0), .Register_Address_1(Register__1),
    .Register_Address_2(Register__2));
  nor NOR (NOR_out, mfhi, rnd, Inp, mflo);
  assign Data_Bus = NOR_out ? ALU_Out : 32'bz;  // Controlled_Buffer controlled_buffer_5
  and and_2 (and_2_out, Memory_Get, ~Push_Pop);  // AND_Gate
  or or_1 (or_1_out, Memory_Get, Memory_Set);
  or or_2 (Rf__Select, Inmediate_Op, and_2_out);
  or or_3 (ALU_Select, Memory_Set, Memory_Get, Inmediate_Op);
  and and_3 (Out_Select, or_1_out, ~Push_Pop);  // AND_Gate
  and and_4 (PC_Select, Clock, ~Push_Pop, Enable);  // AND_Gate
  Shifter #(.width(32)) shifter_1 (.in(Readed_data_3), .\dist (5'b00010), .out(shifter_1_out));
  Multiplexer #(.width(32), .enable("false")) multiplexer_1 (
    .in0(Readed_data_2), .in1(Readed_data_3), .out(multiplexer_1_out), .sel(ALU_Select));
  Multiplexer #(.width(32), .enable("false")) multiplexer_2 (
    .in0(shifter_1_out), .in1(R_0), .out(multiplexer_2_out), .sel(JR));
  Multiplexer #(.width(32), .enable("false")) multiplexer_3 (
    .in0(R_0), .in1(ALU_Out), .out(Readed_data), .sel(Out_Select));
  Branch_Control branch_control_1 (
    .Jmp_Inst(Branch_Op), .Source(Next_Instruction), .Jmp_Length(Readed_data_3), .Destino(multiplexer_2_out),
    .A(R_0), .B(Readed_data_2), .Next(branch_control_1_next));
  ALU alu_1 (
    .Num_A(R_0), .Num_B(multiplexer_1_out), .S__Operation(ALU_Op), .Outp__A_Op_B(ALU_Out),
    .Aux__Outp__A_Op_B(ALU_Aux));
  and and_5 (and_5_out, Clock, Write_to_Hi_Lo);
  and and_6 (and_6_out, Clock, Write_to_Hi_Lo);
  Random #(.width(32), .seed(10291023)) Random_Generator (.clk(and_7_out), .next(1'b1), .out(Random), .clr(Reset));
  and and_7 (and_7_out, Clock, Enable);
  Register #(.width(32)) High (.D(ALU_Aux), .en(Enable), .Q(hi), .clk(and_5_out), .clr(Reset));
  Register #(.width(32)) Low (.D(ALU_Out), .en(Enable), .Q(lo), .clk(and_6_out), .clr(Reset));
  Program_Count program_count_1 (
    .clock(PC_Select), .data(branch_control_1_next), .reset(Reset), .Output(Next_Instruction));
  Multiplexer #(.width(5), .enable("false")) multiplexer_4 (
    .in0(Register__2), .in1(Register__1), .out(multiplexer_4_out), .sel(Rf__Select));
  Register_File register_file_1 (
    .Write_1___Read_0(R_W_Select), .Reset(Reset), .Clock(Clock), .in_4(Data_Bus), .S__Output_A(Register__0),
    .S__Output_B(Register__1), .S__Register_to_Write(multiplexer_4_out), .Output_A(R_0),
    .Output_B(Readed_data_2));

  // Other names for the same wires on the sheet: CLK = Clock; Const[31:0] = Readed_data_3; Input[31:0] = Input_Data;
  //   Ins[31:0] = Instruction; Next_Inst[31:0] = Next_Instruction; R_1[31:0] = Readed_data_2; RST = Reset

  // Notes on the sheet:
  //   Inputs
  //   Selectors
  //   Instruction Decoding
  //   ALU
  //   Outputs
  //   Other Registers
  //   Branch Management
  //   Registers
endmodule

module Control_Unit (
  input  Kbd_Available,
  input  [31:0] RAM_Out_0,
  input  [6:0] Kbd_ASCII_Data,
  input  Reset,
  input  Clock,
  input  End_Cache,
  input  [31:0] Next_Instruction,
  input  [31:0] R_0,
  input  [31:0] R_1,
  input  [31:0] R_2,
  output Start_Cache,
  output Execute_Instruction,
  output [31:0] Data_Output,
  output Cache_R_W,
  output Stop,
  output [31:0] Current_Instruction,
  output TTY_Enable,
  output [6:0] TTY_ASCII_Data,
  output [31:0] ADDRESS,
  output Kbd_Enable
);

  wire add_to_esp, AFTER_W_2_q, and_1_out, and_4_out, comparator_3_eq, comparator_4_eq, comparator_5_eq,
       continue_0, continue_1, demultiplexer_2_out0, demultiplexer_4_out1, demultiplexer_5_out0,
       demultiplexer_7_out1, end_execution, end_execution_0, end_execution_2, end_execution_4,
       end_execution_5, end_execution_6, execute_7, get_inst, get_next_inst, get_set_word, get_set_word_0,
       IDLE_q, Input___cache, Ins, ins____halt__tty__rnd__kbd, ins___halt, ins___kbd, ins___lw, ins___pop,
       ins___push, ins___push____ins___sw, ins___sw, ins___tty, not_1_out, or_1_out, or_2_out, or_6_out,
       ram_get_inst, rset_get_inst, rset_writing, set_block_0, set_esp, sub_to_esp, WHILE_q, writing;
  wire [31:0] adder_1_out, bit_extender_1_out, controlled_buffer_5_out, multiplexer_1_out, multiplexer_2_out;

  Demultiplexer #(.enable("false")) demultiplexer_1 (
    .out0(continue_1), .out1(get_set_word_0), .in(continue_0), .sel(ram_get_inst));
  Demultiplexer #(.enable("false")) demultiplexer_2 (
    .out0(demultiplexer_2_out0), .out1(set_esp), .in(IDLE_q), .sel(and_1_out));
  D_Flip_Flop #(.trigger("falling")) IDLE (
    .clk(Clock), .D(demultiplexer_2_out0), .Q(IDLE_q), .preset(Reset));  // open: Qn, en, reset
  and and_1 (and_1_out, Clock, ~Reset);  // AND_Gate
  and and_2 (set_block_0, End_Cache, ~writing, get_inst);  // AND_Gate
  Demultiplexer #(.enable("false")) demultiplexer_3 (
    .out0(end_execution_0), .out1(Cache_R_W), .in(continue_1), .sel(ins___push____ins___sw));
  assign bit_extender_1_out = {{25{1'b0}}, Kbd_ASCII_Data};  // Bit_Extender bit_extender_1
  not not_1 (not_1_out, Kbd_Available);
  Adder #(.width(32)) adder_1 (.a(R_0), .b(multiplexer_1_out), .out(adder_1_out));  // open: cin, cout
  Multiplexer #(.width(32), .enable("false")) multiplexer_1 (
    .in0({32{1'b0}}), .in1(32'hfffffffc), .out(multiplexer_1_out), .sel(ins___push));
  assign Data_Output = Input___cache ? RAM_Out_0 : 32'bz;  // Controlled_Buffer controlled_buffer_1
  Multiplexer #(.width(32), .enable("false")) multiplexer_2 (
    .in0(bit_extender_1_out), .in1({32{1'b1}}), .out(multiplexer_2_out), .sel(not_1_out));
  assign Data_Output = Kbd_Enable ? multiplexer_2_out : 32'bz;  // Controlled_Buffer controlled_buffer_2
  assign ADDRESS = get_set_word ? adder_1_out : 32'bz;  // Controlled_Buffer controlled_buffer_3
  or or_1 (or_1_out, end_execution, set_esp);
  D_Flip_Flop #(.trigger("falling")) AFTER_W (
    .clk(Clock), .D(set_block_0), .Q(Ins), .reset(Reset));  // open: Qn, preset, en
  assign ADDRESS = get_next_inst ? Next_Instruction : 32'bz;  // Controlled_Buffer controlled_buffer_4
  D_Flip_Flop #(.trigger("falling")) WHILE (
    .clk(Clock), .D(or_1_out), .Q(WHILE_q), .reset(Reset));  // open: Qn, preset, en
  Demultiplexer #(.enable("false")) demultiplexer_4 (
    .out0(get_next_inst), .out1(demultiplexer_4_out1), .in(WHILE_q), .sel(ins___halt));
  D_Flip_Flop #(.trigger("falling")) AFTER_W_2 (
    .clk(Clock), .D(Ins), .Q(AFTER_W_2_q), .reset(Reset));  // open: Qn, preset, en
  Demultiplexer #(.enable("false")) demultiplexer_5 (
    .out0(demultiplexer_5_out0), .out1(TTY_Enable), .in(AFTER_W_2_q), .sel(ins___tty));
  and and_3 (Input___cache, End_Cache, ~writing, ~get_inst);  // AND_Gate
  or or_2 (or_2_out, demultiplexer_4_out1, Stop);
  D_Flip_Flop END (.clk(Clock), .D(or_2_out), .Q(Stop), .reset(Reset));  // open: Qn, preset, en
  Demultiplexer #(.enable("false")) demultiplexer_6 (
    .out0(end_execution_2), .out1(execute_7), .in(Input___cache), .sel(ins___pop));
  and and_4 (and_4_out, End_Cache, writing, ~get_inst);  // AND_Gate
  Comparator #(.width(7), .mode("unsigned")) comparator_1 (
    .a({Current_Instruction[31:26], Current_Instruction[0]}), .b(7'b1110001), .eq(ins___push));  // open: gt, lt
  Comparator #(.width(7), .mode("unsigned")) comparator_2 (
    .a({Current_Instruction[31:26], Current_Instruction[0]}), .b(7'b1110000), .eq(ins___pop));  // open: gt, lt
  Comparator #(.width(6), .mode("unsigned")) comparator_3 (
    .a(Current_Instruction[5:0]), .b({6{1'b1}}), .eq(comparator_3_eq));  // open: gt, lt
  Comparator #(.width(6), .mode("unsigned")) comparator_4 (
    .a(Current_Instruction[5:0]), .b(6'b000001), .eq(comparator_4_eq));  // open: gt, lt
  Comparator #(.width(6), .mode("unsigned")) comparator_5 (
    .a(Current_Instruction[5:0]), .b(6'b000100), .eq(comparator_5_eq));  // open: gt, lt
  Demultiplexer #(.enable("false")) demultiplexer_7 (
    .out0(end_execution_5), .out1(demultiplexer_7_out1), .in(and_4_out), .sel(ins___push));
  and and_5 (ins___halt, comparator_3_eq, ins____halt__tty__rnd__kbd);
  and and_6 (ins___tty, comparator_4_eq, ins____halt__tty__rnd__kbd);
  and and_7 (ins___kbd, comparator_5_eq, ins____halt__tty__rnd__kbd);
  D_Flip_Flop #(.trigger("falling")) d_ff_1 (
    .clk(Clock), .D(execute_7), .Q(add_to_esp), .reset(Reset));  // open: Qn, preset, en
  D_Flip_Flop #(.trigger("falling")) d_ff_2 (
    .clk(Clock), .D(demultiplexer_7_out1), .Q(sub_to_esp), .reset(Reset));  // open: Qn, preset, en
  Demultiplexer #(.enable("false")) demultiplexer_8 (
    .out0(continue_0), .out1(Kbd_Enable), .in(demultiplexer_5_out0), .sel(ins___kbd));
  D_Flip_Flop #(.trigger("falling")) AFTER_W_3 (
    .clk(Clock), .D(add_to_esp), .Q(end_execution_6), .reset(Reset));  // open: Qn, preset, en
  D_Flip_Flop #(.trigger("falling")) d_ff_3 (
    .clk(Clock), .D(sub_to_esp), .Q(end_execution_4), .reset(Reset));  // open: Qn, preset, en
  Comparator #(.width(6), .mode("unsigned")) comparator_6 (
    .a(Current_Instruction[31:26]), .b(6'b100011), .eq(ins___lw));  // open: gt, lt
  Comparator #(.width(6), .mode("unsigned")) comparator_7 (
    .a(Current_Instruction[31:26]), .b(6'b101011), .eq(ins___sw));  // open: gt, lt
  or or_3 (ins___push____ins___sw, ins___sw, ins___push);
  Comparator #(.width(6), .mode("unsigned")) comparator_8 (
    .a(Current_Instruction[31:26]), .b({6{1'b1}}), .eq(ins____halt__tty__rnd__kbd));  // open: gt, lt
  D_Flip_Flop Get_Instruction (.Q(get_inst), .preset(get_next_inst), .reset(rset_get_inst));  // open: clk, D, Qn, en
  D_Flip_Flop u_Writing (.Q(writing), .preset(Cache_R_W), .reset(rset_writing));  // open: clk, D, Qn, en
  or or_4 (Execute_Instruction, end_execution_0, TTY_Enable, end_execution_2, Kbd_Enable, end_execution_4, end_execution_5, end_execution_6, execute_7);
  or or_5 (end_execution, end_execution_0, TTY_Enable, end_execution_2, Kbd_Enable, end_execution_4, end_execution_5, end_execution_6);
  assign controlled_buffer_5_out = Ins ? RAM_Out_0 : 32'bz;  // Controlled_Buffer controlled_buffer_5
  assign controlled_buffer_5_out = sub_to_esp ? 32'h23fffffc : 32'bz;  // Controlled_Buffer controlled_buffer_6
  assign controlled_buffer_5_out = add_to_esp ? 32'h23ff0004 : 32'bz;  // Controlled_Buffer controlled_buffer_7
  or or_6 (or_6_out, Ins, sub_to_esp, add_to_esp);
  Register #(.width(32)) Instruction (
    .D(controlled_buffer_5_out), .en(or_6_out), .Q(Current_Instruction), .clk(Clock), .clr(Reset));
  or or_7 (ram_get_inst, ins___pop, ins___lw);
  or or_8 (get_set_word, get_set_word_0, Cache_R_W);
  or or_9 (Start_Cache, get_next_inst, get_set_word_0, Cache_R_W);
  or or_10 (rset_get_inst, get_set_word_0, Cache_R_W);
  or or_11 (rset_writing, get_set_word_0, get_next_inst);

  // Other names for the same wires on the sheet: addr[31:0] = ADDRESS; CLK = Clock; CLR = Reset;
  //   execute = Execute_Instruction; execute_0 = end_execution_0; end_execution_1 = TTY_Enable;
  //   execute_1 = TTY_Enable; execute_2 = end_execution_2; end_execution_3 = Kbd_Enable; execute_3 = Kbd_Enable;
  //   Input___kbd = Kbd_Enable; execute_4 = end_execution_4; execute_5 = end_execution_5; execute_6 = end_execution_6;
  //   KBD_AVAIL = Kbd_Available; KBD_DATA[6:0] = Kbd_ASCII_Data; next_inst[31:0] = Next_Instruction;
  //   offset[31:0] = R_2; OUT[31:0] = Data_Output; RAM_OUTPUT_0[31:0] = RAM_Out_0; Rs[31:0] = R_0; Rt[31:0] = R_1;
  //   set_block_1 = Input___cache; set_readed = set_block_0; rset_writing_0 = get_next_inst;
  //   set_get_inst = get_next_inst; start_cache_0 = get_next_inst; rset_get_inst_0 = get_set_word_0;
  //   rset_writing_1 = get_set_word_0; start_cache_1 = get_set_word_0; get_set_word_1 = Cache_R_W;
  //   rset_get_inst_1 = Cache_R_W; set_writing = Cache_R_W; start_cache_2 = Cache_R_W; TTY_DATA[6:0] = TTY_ASCII_Data

  // Notes on the sheet:
  //   Data to Out
  //   Instruction to Out
  //   Data from RAM
  //   Sequencing
  //   Inputs
  //   Input Registers
  //   Outputs
  //   Cache
  //   Keyboard
  //   Instruction
  //   Management
  //   TTY & KBD
  //   Sequence
  //   Instruction
  //   Idle/End
  //   Data Buses
  //   Intruction Executer
  //   POP/LW
  //   PUSH/SW
  //   Conditionals
  //   Instruction Get
  //   TTY EXECUTE
  //   KBD
  //   Extra Registers
  //   Same Commands
endmodule

module Cache_128_bytes (
  input  [31:0] Address,
  input  Clock,
  input  Reset,
  input  Start,
  input  nR_W,
  input  [31:0] Data_Path_Value,
  input  [31:0] RAM_Output,
  input  [31:0] RAM_Output_2,
  input  [31:0] RAM_Output_3,
  input  [31:0] RAM_Output_4,
  input  [3:0] Read_Time,
  input  [3:0] Write_Time,
  output [31:0] Output,
  output End,
  output [15:0] RAM_Address,
  output [31:0] RAM_Input,
  output CS,
  output nR_W_2,
  output [3:0] RAM_Mask
);

  wire allow_writing, allow_writing_0, and_1_out, and_2_out, and_3_out, and_4_out, clk, end_0, end_1, line_0,
       line_1, line_2, line_3, line_4, line_5, line_6, line_7, not_1_out, not_2_out, not_3_out, not_4_out,
       not_5_out, or_2_out, or_7_out, or_8_out, or_11_out, or_12_out, or_13_out, or_14_out, or_15_out,
       or_16_out, or_17_out, or_18_out, read_condition, set_valid_0, set_valid_1, set_valid_2, set_valid_3,
       set_valid_4, set_valid_5, set_valid_6, set_valid_7, store_addr, store_addr_0, store_addr_1,
       tag_matches, valid, valid_0, valid_1, valid_2, valid_3, valid_4, valid_5, valid_6, valid_7, wait___0,
       wait_minus_minus, WHILE_2_q, WHILE_q;
  wire [1:0] offset;
  wire [2:0] cache_line;
  wire [3:0] multiplexer_1_out, \wait ;
  wire [15:0] current_tag, set_tag, tag_0, tag_1, tag_2, tag_3, tag_4, tag_5, tag_6, tag_7;
  wire [15:3] mem_block;
  wire [31:0] Data_0, Data_1, Data_2, Data_3, multiplexer_2_out, multiplexer_3_out, multiplexer_4_out,
       multiplexer_5_out, multiplexer_14_out, out_0, out_1, out_2, out_3, remain, stored_addr, val_0_0,
       val_0_1, val_0_2, val_0_3, val_1_0, val_1_1, val_1_2, val_1_3, val_2_0, val_2_1, val_2_2, val_2_3,
       val_3_0, val_3_1, val_3_2, val_3_3, val_4_0, val_4_1, val_4_2, val_4_3, val_5_0, val_5_1, val_5_2,
       val_5_3, val_6_0, val_6_1, val_6_2, val_6_3, val_7_0, val_7_1, val_7_2, val_7_3;
  wire [31:2] divider_2_out;
  wire [31:16] divider_1_out;

  not not_1 (not_1_out, nR_W_2);
  and and_1 (and_1_out, Clock, not_1_out, allow_writing);
  and and_2 (and_2_out, Clock, valid, allow_writing);
  assign RAM_Address = CS ? {mem_block, cache_line} : 16'bz;  // Controlled_Buffer controlled_buffer_1
  assign set_tag = wait___0 ? {mem_block, cache_line} : 16'bz;  // Controlled_Buffer controlled_buffer_2
  or or_1 (clk, and_1_out, and_2_out);
  Multiplexer #(.width(4), .enable("false")) multiplexer_1 (
    .in0(Read_Time), .in1(Write_Time), .out(multiplexer_1_out), .sel(nR_W));
  not not_2 (not_2_out, wait___0);
  Multiplexer #(.width(32), .enable("false")) multiplexer_2 (
    .in0(out_0), .in1(Data_Path_Value), .out(multiplexer_2_out), .sel(RAM_Mask[0]));
  Multiplexer #(.width(32), .enable("false")) multiplexer_3 (
    .in0(out_1), .in1(Data_Path_Value), .out(multiplexer_3_out), .sel(RAM_Mask[1]));
  Multiplexer #(.width(32), .enable("false")) multiplexer_4 (
    .in0(out_2), .in1(Data_Path_Value), .out(multiplexer_4_out), .sel(RAM_Mask[2]));
  Multiplexer #(.width(32), .enable("false")) multiplexer_5 (
    .in0(out_3), .in1(Data_Path_Value), .out(multiplexer_5_out), .sel(RAM_Mask[3]));
  Register #(.width(32)) MEM_ADDR (.D(Address), .en(store_addr), .Q(stored_addr), .clk(Clock), .clr(Reset));
  or or_2 (or_2_out, store_addr, wait_minus_minus);
  Counter #(.width(4), .max('hf), .trigger("falling")) u_WAIT (
    .load(or_2_out), .D(multiplexer_1_out), .count(wait_minus_minus), .Q(\wait ), .clk(Clock), .clr(Reset));  // open: carry
  Divider #(.width(32)) divider_1 (
    .a(stored_addr), .b(32'h10), .out({divider_1_out, mem_block, cache_line}), .rem(remain));  // open: upper
  Divider #(.width(32)) divider_2 (.a(remain), .b(32'h4), .out({divider_2_out, offset}));  // open: upper, rem
  Decoder #(.select(3), .enable("false")) decoder_1 (
    .out0(line_0), .out1(line_1), .out2(line_2), .out3(line_3), .out4(line_4), .out5(line_5), .out6(line_6),
    .out7(line_7), .sel(cache_line));
  Comparator #(.width(16), .mode("unsigned")) comparator_1 (
    .a(current_tag), .b({mem_block, cache_line}), .eq(tag_matches));  // open: gt, lt
  Comparator #(.width(4), .mode("unsigned")) comparator_2 (.a(\wait ), .b(4'b0000), .eq(wait___0));  // open: gt, lt
  not not_3 (not_3_out, tag_matches);
  not not_4 (not_4_out, valid);
  Multiplexer #(.width(32), .enable("false")) multiplexer_6 (
    .in0(RAM_Output), .in1(multiplexer_2_out), .out(Data_0), .sel(nR_W_2));
  Multiplexer #(.width(32), .enable("false")) multiplexer_7 (
    .in0(RAM_Output_2), .in1(multiplexer_3_out), .out(Data_1), .sel(nR_W_2));
  Multiplexer #(.width(32), .enable("false")) multiplexer_8 (
    .in0(RAM_Output_3), .in1(multiplexer_4_out), .out(Data_2), .sel(nR_W_2));
  Multiplexer #(.width(32), .enable("false")) multiplexer_9 (
    .in0(RAM_Output_4), .in1(multiplexer_5_out), .out(Data_3), .sel(nR_W_2));
  Decoder #(.select(2), .enable("false")) decoder_2 (
    .out0(RAM_Mask[0]), .out1(RAM_Mask[1]), .out2(RAM_Mask[2]), .out3(RAM_Mask[3]), .sel(offset));
  and and_3 (and_3_out, not_2_out, not_3_out);
  or or_3 (read_condition, and_3_out, and_4_out);
  and and_4 (and_4_out, not_2_out, not_4_out);
  Demultiplexer #(.select(3), .enable("false")) demultiplexer_1 (
    .out0(set_valid_0), .out1(set_valid_1), .out2(set_valid_2), .out3(set_valid_3), .out4(set_valid_4),
    .out5(set_valid_5), .out6(set_valid_6), .out7(set_valid_7), .in(end_0), .sel(cache_line));
  Multiplexer #(.select(3), .width(32), .enable("false")) multiplexer_10 (
    .in0(val_0_0), .in1(val_1_0), .in2(val_2_0), .in3(val_3_0), .in4(val_4_0), .in5(val_5_0), .in6(val_6_0),
    .in7(val_7_0), .out(out_0), .sel(cache_line));
  Multiplexer #(.select(3), .width(32), .enable("false")) multiplexer_11 (
    .in0(val_0_1), .in1(val_1_1), .in2(val_2_1), .in3(val_3_1), .in4(val_4_1), .in5(val_5_1), .in6(val_6_1),
    .in7(val_7_1), .out(out_1), .sel(cache_line));
  Multiplexer #(.select(3), .width(32), .enable("false")) multiplexer_12 (
    .in0(val_0_2), .in1(val_1_2), .in2(val_2_2), .in3(val_3_2), .in4(val_4_2), .in5(val_5_2), .in6(val_6_2),
    .in7(val_7_2), .out(out_2), .sel(cache_line));
  Multiplexer #(.select(3), .width(32), .enable("false")) multiplexer_13 (
    .in0(val_0_3), .in1(val_1_3), .in2(val_2_3), .in3(val_3_3), .in4(val_4_3), .in5(val_5_3), .in6(val_6_3),
    .in7(val_7_3), .out(out_3), .sel(cache_line));
  Multiplexer #(.select(2), .width(32), .enable("false")) multiplexer_14 (
    .in0(out_0), .in1(out_1), .in2(out_2), .in3(out_3), .out(multiplexer_14_out), .sel(offset));
  Add_Endiannes add_endiannes_1 (.Input(multiplexer_14_out), .Output(Output));
  Multiplexer #(.select(3), .width(16), .enable("false")) multiplexer_15 (
    .in0(tag_0), .in1(tag_1), .in2(tag_2), .in3(tag_3), .in4(tag_4), .in5(tag_5), .in6(tag_6), .in7(tag_7),
    .out(current_tag), .sel(cache_line));
  Multiplexer #(.select(3), .enable("false")) multiplexer_16 (
    .in0(valid_0), .in1(valid_1), .in2(valid_2), .in3(valid_3), .in4(valid_4), .in5(valid_5), .in6(valid_6),
    .in7(valid_7), .out(valid), .sel(cache_line));
  and and_5 (store_addr_0, Start, ~nR_W);  // AND_Gate
  and and_6 (store_addr_1, Start, nR_W);
  or or_4 (End, end_0, end_1);
  or or_5 (wait_minus_minus, allow_writing_0, nR_W_2);
  or or_6 (store_addr, store_addr_0, store_addr_1);
  or or_7 (or_7_out, store_addr_0, allow_writing_0);
  or or_8 (or_8_out, store_addr_1, nR_W_2);
  Demultiplexer #(.enable("false")) demultiplexer_2 (
    .out0(end_0), .out1(allow_writing_0), .in(WHILE_q), .sel(read_condition));
  D_Flip_Flop #(.trigger("falling")) WHILE (
    .clk(Clock), .D(or_7_out), .Q(WHILE_q), .reset(Reset));  // open: Qn, preset, en
  D_Flip_Flop #(.trigger("falling")) WHILE_2 (
    .clk(Clock), .D(or_8_out), .Q(WHILE_2_q), .reset(Reset));  // open: Qn, preset, en
  Demultiplexer #(.enable("false")) demultiplexer_3 (.out0(end_1), .out1(nR_W_2), .in(WHILE_2_q), .sel(not_5_out));
  not not_5 (not_5_out, wait___0);
  or or_9 (allow_writing, allow_writing_0, nR_W_2);
  or or_10 (CS, allow_writing_0, nR_W_2);
  or or_11 (or_11_out, valid_0, set_valid_0);
  or or_12 (or_12_out, valid_1, set_valid_1);
  or or_13 (or_13_out, valid_2, set_valid_2);
  or or_14 (or_14_out, valid_3, set_valid_3);
  or or_15 (or_15_out, valid_4, set_valid_4);
  or or_16 (or_16_out, valid_5, set_valid_5);
  or or_17 (or_17_out, valid_6, set_valid_6);
  or or_18 (or_18_out, valid_7, set_valid_7);
  D_Flip_Flop #(.trigger("falling")) d_ff_1 (
    .clk(Clock), .D(or_11_out), .Q(valid_0), .reset(Reset));  // open: Qn, preset, en
  D_Flip_Flop #(.trigger("falling")) d_ff_2 (
    .clk(Clock), .D(or_12_out), .Q(valid_1), .reset(Reset));  // open: Qn, preset, en
  D_Flip_Flop #(.trigger("falling")) d_ff_3 (
    .clk(Clock), .D(or_13_out), .Q(valid_2), .reset(Reset));  // open: Qn, preset, en
  D_Flip_Flop #(.trigger("falling")) d_ff_4 (
    .clk(Clock), .D(or_14_out), .Q(valid_3), .reset(Reset));  // open: Qn, preset, en
  D_Flip_Flop #(.trigger("falling")) d_ff_5 (
    .clk(Clock), .D(or_15_out), .Q(valid_4), .reset(Reset));  // open: Qn, preset, en
  D_Flip_Flop #(.trigger("falling")) d_ff_6 (
    .clk(Clock), .D(or_16_out), .Q(valid_5), .reset(Reset));  // open: Qn, preset, en
  D_Flip_Flop #(.trigger("falling")) d_ff_7 (
    .clk(Clock), .D(or_17_out), .Q(valid_6), .reset(Reset));  // open: Qn, preset, en
  D_Flip_Flop #(.trigger("falling")) d_ff_8 (
    .clk(Clock), .D(or_18_out), .Q(valid_7), .reset(Reset));  // open: Qn, preset, en
  Register #(.width(16), .trigger("falling")) register_1 (.D(set_tag), .en(line_0), .Q(tag_0), .clk(clk), .clr(Reset));
  Register #(.width(16), .trigger("falling")) register_2 (.D(set_tag), .en(line_1), .Q(tag_1), .clk(clk), .clr(Reset));
  Register #(.width(16), .trigger("falling")) register_3 (.D(set_tag), .en(line_2), .Q(tag_2), .clk(clk), .clr(Reset));
  Register #(.width(16), .trigger("falling")) register_4 (.D(set_tag), .en(line_3), .Q(tag_3), .clk(clk), .clr(Reset));
  Register #(.width(16), .trigger("falling")) register_5 (.D(set_tag), .en(line_4), .Q(tag_4), .clk(clk), .clr(Reset));
  Register #(.width(16), .trigger("falling")) register_6 (.D(set_tag), .en(line_5), .Q(tag_5), .clk(clk), .clr(Reset));
  Register #(.width(16), .trigger("falling")) register_7 (.D(set_tag), .en(line_6), .Q(tag_6), .clk(clk), .clr(Reset));
  Register #(.width(16), .trigger("falling")) register_8 (.D(set_tag), .en(line_7), .Q(tag_7), .clk(clk), .clr(Reset));
  Register #(.width(32), .trigger("falling")) register_9 (.D(Data_0), .en(line_0), .Q(val_0_0), .clk(clk), .clr(Reset));
  Register #(.width(32), .trigger("falling")) register_10 (
    .D(Data_0), .en(line_1), .Q(val_1_0), .clk(clk), .clr(Reset));
  Register #(.width(32), .trigger("falling")) register_11 (
    .D(Data_0), .en(line_2), .Q(val_2_0), .clk(clk), .clr(Reset));
  Register #(.width(32), .trigger("falling")) register_12 (
    .D(Data_0), .en(line_3), .Q(val_3_0), .clk(clk), .clr(Reset));
  Register #(.width(32), .trigger("falling")) register_13 (
    .D(Data_0), .en(line_4), .Q(val_4_0), .clk(clk), .clr(Reset));
  Register #(.width(32), .trigger("falling")) register_14 (
    .D(Data_0), .en(line_5), .Q(val_5_0), .clk(clk), .clr(Reset));
  Register #(.width(32), .trigger("falling")) register_15 (
    .D(Data_0), .en(line_6), .Q(val_6_0), .clk(clk), .clr(Reset));
  Register #(.width(32), .trigger("falling")) register_16 (
    .D(Data_0), .en(line_7), .Q(val_7_0), .clk(clk), .clr(Reset));
  Register #(.width(32), .trigger("falling")) register_17 (
    .D(Data_1), .en(line_0), .Q(val_0_1), .clk(clk), .clr(Reset));
  Register #(.width(32), .trigger("falling")) register_18 (
    .D(Data_1), .en(line_1), .Q(val_1_1), .clk(clk), .clr(Reset));
  Register #(.width(32), .trigger("falling")) register_19 (
    .D(Data_1), .en(line_2), .Q(val_2_1), .clk(clk), .clr(Reset));
  Register #(.width(32), .trigger("falling")) register_20 (
    .D(Data_1), .en(line_3), .Q(val_3_1), .clk(clk), .clr(Reset));
  Register #(.width(32), .trigger("falling")) register_21 (
    .D(Data_1), .en(line_4), .Q(val_4_1), .clk(clk), .clr(Reset));
  Register #(.width(32), .trigger("falling")) register_22 (
    .D(Data_1), .en(line_5), .Q(val_5_1), .clk(clk), .clr(Reset));
  Register #(.width(32), .trigger("falling")) register_23 (
    .D(Data_1), .en(line_6), .Q(val_6_1), .clk(clk), .clr(Reset));
  Register #(.width(32), .trigger("falling")) register_24 (
    .D(Data_1), .en(line_7), .Q(val_7_1), .clk(clk), .clr(Reset));
  Register #(.width(32), .trigger("falling")) register_25 (
    .D(Data_2), .en(line_0), .Q(val_0_2), .clk(clk), .clr(Reset));
  Register #(.width(32), .trigger("falling")) register_26 (
    .D(Data_2), .en(line_1), .Q(val_1_2), .clk(clk), .clr(Reset));
  Register #(.width(32), .trigger("falling")) register_27 (
    .D(Data_2), .en(line_2), .Q(val_2_2), .clk(clk), .clr(Reset));
  Register #(.width(32), .trigger("falling")) register_28 (
    .D(Data_2), .en(line_3), .Q(val_3_2), .clk(clk), .clr(Reset));
  Register #(.width(32), .trigger("falling")) register_29 (
    .D(Data_2), .en(line_4), .Q(val_4_2), .clk(clk), .clr(Reset));
  Register #(.width(32), .trigger("falling")) register_30 (
    .D(Data_2), .en(line_5), .Q(val_5_2), .clk(clk), .clr(Reset));
  Register #(.width(32), .trigger("falling")) register_31 (
    .D(Data_2), .en(line_6), .Q(val_6_2), .clk(clk), .clr(Reset));
  Register #(.width(32), .trigger("falling")) register_32 (
    .D(Data_2), .en(line_7), .Q(val_7_2), .clk(clk), .clr(Reset));
  Register #(.width(32), .trigger("falling")) register_33 (
    .D(Data_3), .en(line_0), .Q(val_0_3), .clk(clk), .clr(Reset));
  Register #(.width(32), .trigger("falling")) register_34 (
    .D(Data_3), .en(line_1), .Q(val_1_3), .clk(clk), .clr(Reset));
  Register #(.width(32), .trigger("falling")) register_35 (
    .D(Data_3), .en(line_2), .Q(val_2_3), .clk(clk), .clr(Reset));
  Register #(.width(32), .trigger("falling")) register_36 (
    .D(Data_3), .en(line_3), .Q(val_3_3), .clk(clk), .clr(Reset));
  Register #(.width(32), .trigger("falling")) register_37 (
    .D(Data_3), .en(line_4), .Q(val_4_3), .clk(clk), .clr(Reset));
  Register #(.width(32), .trigger("falling")) register_38 (
    .D(Data_3), .en(line_5), .Q(val_5_3), .clk(clk), .clr(Reset));
  Register #(.width(32), .trigger("falling")) register_39 (
    .D(Data_3), .en(line_6), .Q(val_6_3), .clk(clk), .clr(Reset));
  Register #(.width(32), .trigger("falling")) register_40 (
    .D(Data_3), .en(line_7), .Q(val_7_3), .clk(clk), .clr(Reset));

  assign RAM_Input = Data_Path_Value;

  // Other names for the same wires on the sheet: mem_block[2:0] = cache_line; tag[15:0] = {mem_block, cache_line};
  //   addr[31:0] = Address; clk_ = Clock; DPath_in[31:0] = Data_Path_Value; msk[3:0] = RAM_Mask; msk0 = RAM_Mask[0];
  //   msk1 = RAM_Mask[1]; msk2 = RAM_Mask[2]; msk3 = RAM_Mask[3]; out[31:0] = Output; r_w = nR_W;
  //   RAM_Out_0[31:0] = RAM_Output; RAM_Out_1[31:0] = RAM_Output_2; RAM_Out_2[31:0] = RAM_Output_3;
  //   RAM_Out_3[31:0] = RAM_Output_4; rst = Reset; rt[3:0] = Read_Time; set_valid = end_0; CS_0 = allow_writing_0;
  //   wait___0_t = allow_writing_0; _r_w = nR_W_2; allow_writing_1 = nR_W_2; CS_1 = nR_W_2; wait___1 = nR_W_2;
  //   wt[3:0] = Write_Time
endmodule
